// Logisim project m1.HPC.S2.MOHAMMEDI.PROJET.ARSHI-juste.circ as structural Verilog: 4 circuits, main circuit main
// UAL
module main (
  input  in_1,
  input  in_2
);

  wire clock_1_out, control_begin_1_out_10;
  wire [3:0] control_begin_1_out_4, control_begin_1_out_5, control_begin_1_out_6, control_begin_1_out_7;
  wire [7:0] control_begin_1__8bit_minus;
  wire [15:0] control_begin_1_out_8, ram_1_data, registre_file_16_bit_1_out_7, registre_file_16_bit_1_out_8,
       ual_1bit_1_resulta;

  RAM #(.addrWidth(16), .dataWidth(16), .bus("separate")) ram_1 (
    .addr(control_begin_1_out_8), .data(ram_1_data), .ld(1'b1), .clr(in_1));  // open: din, str, sel, clk
  Clock clock_1 (.out(clock_1_out));
  control_begin control_begin_1 (
    .in_1(ram_1_data), ._8BIT_minus(control_begin_1__8bit_minus), .out_4(control_begin_1_out_4),
    .out_5(control_begin_1_out_5), .out_6(control_begin_1_out_6), .out_7(control_begin_1_out_7),
    .out_8(control_begin_1_out_8), .out_10(control_begin_1_out_10), .in_2(clock_1_out));  // open: out_9
  registre_file_16_bit registre_file_16_bit_1 (
    .HORLOGE(in_2), .DONNER(ual_1bit_1_resulta), .AO(control_begin_1_out_6),
    .out_7(registre_file_16_bit_1_out_7), .out_8(registre_file_16_bit_1_out_8), .A1(control_begin_1_out_4),
    .A2(control_begin_1_out_5), .in_4(control_begin_1_out_10));
  ual_1BIT ual_1bit_1 (
    .A(registre_file_16_bit_1_out_7), .B(registre_file_16_bit_1_out_8), .OPPERATION(control_begin_1_out_7),
    .resulta(ual_1bit_1_resulta), .in_4(control_begin_1__8bit_minus));
endmodule

module ual_1BIT (
  input  [15:0] B,
  input  [15:0] A,
  input  [3:0] OPPERATION,
  input  [7:0] in_4,
  output [15:0] resulta
);

  wire [15:0] adder_1_out, adder_2_out, adder_3_out, and_1_out, bit_extender_1_out, bit_extender_2_out,
       divider_1_out, multiplier_1_out, not_1_out, or_1_out, subtractor_1_out, undriven, xor_1_out;

  Adder #(.width(16)) adder_1 (.a(B), .b(A), .out(adder_1_out));  // open: cin, cout
  Subtractor #(.width(16)) subtractor_1 (.a(A), .b(B), .out(subtractor_1_out));  // open: bin, bout
  Multiplier #(.width(16)) multiplier_1 (.a(A), .b(B), .out(multiplier_1_out));  // open: cin, cout
  Divider #(.width(16)) divider_1 (.a(A), .b(B), .out(divider_1_out));  // open: upper, rem
  assign and_1_out = A & B;  // AND_Gate and_1, 16 bits wide
  assign or_1_out = A | B;  // OR_Gate or_1, 16 bits wide
  assign xor_1_out = B ^ A;  // XOR_Gate xor_1, 16 bits wide
  assign not_1_out = ~A;  // NOT_Gate not_1, 16 bits wide
  assign bit_extender_1_out = {{8{1'b0}}, in_4};  // Bit_Extender bit_extender_1
  assign bit_extender_2_out = {{8{1'b0}}, in_4};  // Bit_Extender bit_extender_2
  Adder #(.width(16)) adder_2 (.a(bit_extender_1_out), .b(A), .out(adder_2_out));  // open: cin, cout
  Adder #(.width(16)) adder_3 (.a(bit_extender_2_out), .b(B), .out(adder_3_out));  // open: cin, cout
  Multiplexer #(.select(4), .width(16), .enable("false")) multiplexer_1 (
    .in1(adder_1_out), .in2(subtractor_1_out), .in3(multiplier_1_out), .in4(divider_1_out), .in5(and_1_out),
    .in6(or_1_out), .in7(xor_1_out), .in8(not_1_out), .in9(undriven), .in10(undriven), .in14(adder_2_out),
    .in15(adder_3_out), .out(resulta), .sel(OPPERATION));  // open: in0, in11, in12, in13

  // Notes on the sheet:
  //                      data extension
endmodule

// A0
module registre_file_16_bit (
  input  HORLOGE,
  input  [15:0] DONNER,
  input  [3:0] A1,
  input  in_4,
  input  [3:0] AO,
  input  [3:0] A2,
  output [15:0] out_7,
  output [15:0] out_8
);

  wire and_1_out, and_2_out, and_3_out, and_4_out, and_5_out, and_6_out, and_7_out, and_8_out, and_9_out,
       and_10_out, and_11_out, and_12_out, and_13_out, and_14_out, and_15_out, and_16_out, buffer_1_out,
       decoder_1_out0, decoder_1_out1, decoder_1_out2, decoder_1_out3, decoder_1_out4, decoder_1_out5,
       decoder_1_out6, decoder_1_out7, decoder_1_out8, decoder_1_out9, decoder_1_out10, decoder_1_out11,
       decoder_1_out12, decoder_1_out13, decoder_1_out14, decoder_1_out15;
  wire [3:0] multiplexer_3_out;
  wire [15:0] register_1_q, register_2_q, register_3_q, register_4_q, register_5_q, register_6_q,
       register_7_q, register_8_q, register_9_q, register_10_q, register_11_q, register_12_q, register_13_q,
       register_14_q, register_15_q, register_16_q;

  Decoder #(.select(4), .enable("false")) decoder_1 (
    .out0(decoder_1_out0), .out1(decoder_1_out1), .out2(decoder_1_out2), .out3(decoder_1_out3),
    .out4(decoder_1_out4), .out5(decoder_1_out5), .out6(decoder_1_out6), .out7(decoder_1_out7),
    .out8(decoder_1_out8), .out9(decoder_1_out9), .out10(decoder_1_out10), .out11(decoder_1_out11),
    .out12(decoder_1_out12), .out13(decoder_1_out13), .out14(decoder_1_out14), .out15(decoder_1_out15),
    .sel(AO));
  buf buffer_1 (buffer_1_out, HORLOGE);
  Register #(.width(16)) register_1 (.D(DONNER), .Q(register_1_q), .clk(and_1_out));  // open: en, clr
  and and_1 (and_1_out, decoder_1_out0, buffer_1_out);
  Register #(.width(16)) register_2 (.D(DONNER), .Q(register_2_q), .clk(and_2_out));  // open: en, clr
  and and_2 (and_2_out, buffer_1_out, decoder_1_out1);
  Register #(.width(16)) register_3 (.D(DONNER), .Q(register_3_q), .clk(and_3_out));  // open: en, clr
  and and_3 (and_3_out, decoder_1_out2, buffer_1_out);
  Register #(.width(16)) register_4 (.D(DONNER), .Q(register_4_q), .clk(and_4_out));  // open: en, clr
  and and_4 (and_4_out, decoder_1_out3, buffer_1_out);
  Register #(.width(16)) register_5 (.Q(register_5_q), .clk(and_5_out));  // open: D, en, clr
  and and_5 (and_5_out, buffer_1_out, decoder_1_out4);
  Register #(.width(16)) register_6 (.D(DONNER), .Q(register_6_q), .clk(and_6_out));  // open: en, clr
  and and_6 (and_6_out, buffer_1_out, decoder_1_out5);
  Register #(.width(16)) register_7 (.D(DONNER), .Q(register_7_q), .clk(and_7_out));  // open: en, clr
  and and_7 (and_7_out, decoder_1_out6, buffer_1_out);
  Register #(.width(16)) register_8 (.D(DONNER), .Q(register_8_q), .clk(and_8_out));  // open: en, clr
  and and_8 (and_8_out, buffer_1_out, decoder_1_out7);
  and and_9 (and_9_out, decoder_1_out8, buffer_1_out);
  and and_10 (and_10_out, buffer_1_out, decoder_1_out9);
  and and_11 (and_11_out, decoder_1_out10, buffer_1_out);
  and and_12 (and_12_out, decoder_1_out11, buffer_1_out);
  and and_13 (and_13_out, buffer_1_out, decoder_1_out12);
  and and_14 (and_14_out, buffer_1_out, decoder_1_out13);
  and and_15 (and_15_out, decoder_1_out14, buffer_1_out);
  and and_16 (and_16_out, buffer_1_out, decoder_1_out15);
  Register #(.width(16)) register_9 (.D(DONNER), .Q(register_9_q), .clk(and_9_out));  // open: en, clr
  Register #(.width(16)) register_10 (.D(DONNER), .Q(register_10_q), .clk(and_10_out));  // open: en, clr
  Register #(.width(16)) register_11 (.D(DONNER), .Q(register_11_q), .clk(and_11_out));  // open: en, clr
  Register #(.width(16)) register_12 (.D(DONNER), .Q(register_12_q), .clk(and_12_out));  // open: en, clr
  Register #(.width(16)) register_13 (.Q(register_13_q), .clk(and_13_out));  // open: D, en, clr
  Register #(.width(16)) register_14 (.D(DONNER), .Q(register_14_q), .clk(and_14_out));  // open: en, clr
  Register #(.width(16)) register_15 (.D(DONNER), .Q(register_15_q), .clk(and_15_out));  // open: en, clr
  Register #(.width(16)) register_16 (.D(DONNER), .Q(register_16_q), .clk(and_16_out));  // open: en, clr
  Multiplexer #(.select(4), .width(16)) multiplexer_1 (
    .in0(register_1_q), .in1(register_2_q), .in2(register_3_q), .in3(register_4_q), .in4(register_5_q),
    .in5(register_6_q), .in6(register_7_q), .in7(register_8_q), .in8(register_9_q), .in9(register_10_q),
    .in10(register_11_q), .in11(register_12_q), .in12(register_13_q), .in13(register_14_q),
    .in14(register_15_q), .in15(register_16_q), .out(out_7), .sel(multiplexer_3_out));  // open: en
  Multiplexer #(.select(4), .width(16)) multiplexer_2 (
    .in0(register_1_q), .in1(register_2_q), .in2(register_3_q), .in3(register_4_q), .in4(register_5_q),
    .in5(register_6_q), .in6(register_7_q), .in7(register_8_q), .in8(register_9_q), .in9(register_10_q),
    .in10(register_11_q), .in11(register_12_q), .in12(register_13_q), .in13(register_14_q),
    .in14(register_15_q), .in15(register_16_q), .out(out_8), .sel(A2));  // open: en
  Multiplexer #(.width(4), .enable("false")) multiplexer_3 (.in0(A1), .in1(AO), .out(multiplexer_3_out), .sel(in_4));

  // Other names for the same wires on the sheet: A0[3:0] = AO
endmodule

module control_begin (
  input  [15:0] in_1,
  input  in_2,
  output [7:0] _8BIT_minus,
  output [3:0] out_4,
  output [3:0] out_5,
  output [3:0] out_6,
  output [3:0] out_7,
  output [15:0] out_8,
  output out_9,
  output out_10
);

  wire comparator_1_eq, not_1_out;
  wire [15:0] adder_1_out;

  Adder #(.width(16)) adder_1 (.a(out_8), .b(16'h1), .out(adder_1_out));  // open: cin, cout
  Comparator #(.width(16)) comparator_1 (.a(out_8), .b({16{1'b1}}), .eq(comparator_1_eq));  // open: gt, lt
  not not_1 (not_1_out, comparator_1_eq);
  Register #(.width(16)) pc (.D(adder_1_out), .en(not_1_out), .Q(out_8), .clk(in_2));  // open: clr
  buf buffer_1 (out_9, in_1[15]);
  and and_1 (out_10, in_1[12], in_1[14], in_1[15]);

  assign _8BIT_minus = in_1[7:0];
  assign out_4 = in_1[3:0];
  assign out_5 = in_1[7:4];
  assign out_6 = in_1[11:8];
  assign out_7 = in_1[15:12];

  // Notes on the sheet:
  //                    sortie -pc +1
  //   DATA_
  //   HORLOGE REGISTRE FILE
  //                registre-file 2
  //                     Registre file 
  //                    ual-controle
  //   1
  //                      registre file 3
  //                      POUR ECRIRE
  //                     HORLOGE-regisre file
  //                          mux_alu
  //            et distination
endmodule
